// Logisim project Pong.circ as structural Verilog: 5 circuits, main circuit main
module main (
  input  in_1,
  input  [7:0] _0,
  input  in_3,
  input  [7:0] _1,
  input  [7:0] _2,
  input  [7:0] _3,
  input  [7:0] _4,
  input  [7:0] _5,
  input  [7:0] _6,
  input  [7:0] _7,
  input  [7:0] _8,
  input  [7:0] _9,
  input  in_13,
  input  Win,
  output [6:0] out_15
);

  wire and_1_out, and_2_out, and_3_out, and_4_out, and_5_out, and_6_out, and_7_out, and_8_out, and_9_out,
       and_10_out, and_12_out, and_13_out, and_14_out, and_15_out, and_16_out, and_17_out, and_18_out,
       and_19_out, and_20_out, and_21_out, and_22_out, and_23_out, and_24_out, and_25_out, and_26_out,
       and_27_out, and_28_out, and_29_out, and_30_out, and_32_out, and_35_out, and_36_out, and_37_out,
       button_2_out, by, byP1, byP2, clock_2_out, clock_3_out, clock_out, comparator_1_eq, comparator_2_lt,
       comparator_4_eq, comparator_5_lt, counter_3_q, counter_4_q, counter_5_q, loop1, multiplexer_1_out,
       not_1_out, not_2_out, not_3_out, not_4_out, not_5_out, not_6_out, not_7_out, not_8_out, not_9_out,
       not_10_out, not_13_out, not_14_out, or_1_out, or_2_out, or_3_out, or_4_out, or_5_out, or_6_out,
       or_7_out, or_8_out, or_10_out, or_11_out, or_12_out, or_14_out, or_15_out, p2_prime_p1p0_prime, reset,
       S1, S2, S3, S4, S5, S6, S7, score, scoreStop, state0, state1, state2, state2_3, state3, state4,
       state5, state6, state7, xBegin, xEnd, xor_1_out, xor_2_out, yBegin, yEnd;
  wire [2:0] d_ff_3_q;
  wire [3:0] countBall_Y_q, counter_1_q, counter_2_q;
  wire [4:0] countBall_X_q, register_1_q;
  wire [9:0] and_33_out, and_34_out, ball_Y_2_q, ball_Y_q, demultiplexer_1_out1, demultiplexer_1_out2,
       demultiplexer_1_out3, demultiplexer_1_out4, demultiplexer_1_out5, demultiplexer_1_out6,
       demultiplexer_1_out7, demultiplexer_1_out8, demultiplexer_1_out9, demultiplexer_1_out10,
       demultiplexer_1_out11, demultiplexer_1_out12, demultiplexer_1_out13, demultiplexer_1_out14,
       demultiplexer_1_out15, demultiplexer_1_out16, demultiplexer_1_out17, demultiplexer_1_out18,
       demultiplexer_1_out19, multiplexer_3_out, multiplexer_4_out, or_17_out, players_1_outp1,
       players_1_outp2, shifter_1_out, shifter_2_out;

  not not_1 (not_1_out, d_ff_3_q[2]);
  not not_2 (not_2_out, d_ff_3_q[1]);
  not not_3 (not_3_out, d_ff_3_q[0]);
  not not_4 (not_4_out, d_ff_3_q[2]);
  not not_5 (not_5_out, d_ff_3_q[1]);
  not not_6 (not_6_out, d_ff_3_q[0]);
  and and_1 (and_1_out, ~d_ff_3_q[2], ~d_ff_3_q[1], d_ff_3_q[0]);  // AND_Gate
  and and_2 (and_2_out, d_ff_3_q[2], ~d_ff_3_q[1], ~d_ff_3_q[0]);  // AND_Gate
  and and_3 (and_3_out, d_ff_3_q[2], ~d_ff_3_q[1], ~d_ff_3_q[0], byP2, loop1);  // AND_Gate
  and and_4 (and_4_out, d_ff_3_q[2], ~d_ff_3_q[1], ~d_ff_3_q[0], xEnd, ~loop1);  // AND_Gate
  and and_5 (and_5_out, d_ff_3_q[2], d_ff_3_q[1], d_ff_3_q[0], ~reset);  // AND_Gate
  and and_6 (and_6_out, ~d_ff_3_q[2], ~d_ff_3_q[1], ~d_ff_3_q[0], in_1);  // AND_Gate
  and and_7 (and_7_out, loop1, byP1, xBegin);
  and and_8 (and_8_out, ~d_ff_3_q[2], d_ff_3_q[1], d_ff_3_q[0]);  // AND_Gate
  not not_7 (not_7_out, d_ff_3_q[0]);
  and and_9 (and_9_out, ~byP1, byP2);  // AND_Gate
  and and_10 (and_10_out, ~byP2, byP1);  // AND_Gate
  and and_11 (p2_prime_p1p0_prime, not_1_out, not_3_out, d_ff_3_q[1]);
  and and_12 (and_12_out, d_ff_3_q[2], d_ff_3_q[1], ~d_ff_3_q[0], score);  // AND_Gate
  or or_1 (or_1_out, score, and_13_out);
  and and_13 (and_13_out, xEnd, ~loop1, byP2);  // AND_Gate
  and and_14 (and_14_out, xBegin, byP1, not_4_out, d_ff_3_q[1], d_ff_3_q[0], loop1);
  and and_15 (and_15_out, loop1, d_ff_3_q[2], not_5_out, not_6_out, xEnd, byP2);
  and and_16 (and_16_out, d_ff_3_q[2], d_ff_3_q[1], d_ff_3_q[0], ~reset);  // AND_Gate
  or or_2 (or_2_out, and_17_out, and_19_out, score);
  and and_17 (and_17_out, xEnd, ~byP2);  // AND_Gate
  and and_18 (and_18_out, or_2_out, p2_prime_p1p0_prime);
  and and_19 (and_19_out, ~xEnd, ~xBegin, loop1);  // AND_Gate
  and and_20 (and_20_out, ~d_ff_3_q[2], d_ff_3_q[1], d_ff_3_q[0], xBegin, loop1, ~byP1);  // AND_Gate
  and and_21 (and_21_out, d_ff_3_q[2], d_ff_3_q[1], ~d_ff_3_q[0]);  // AND_Gate
  and and_22 (and_22_out, p2_prime_p1p0_prime, or_3_out);
  or or_3 (or_3_out, score, and_23_out);
  and and_23 (and_23_out, xEnd, ~byP2);  // AND_Gate
  and and_24 (and_24_out, ~xBegin, ~xEnd);  // AND_Gate
  or or_4 (or_4_out, and_24_out, and_7_out);
  not not_8 (not_8_out, d_ff_3_q[1]);
  or or_5 (or_5_out, and_9_out, and_10_out);
  and and_25 (and_25_out, or_1_out, p2_prime_p1p0_prime);
  not not_9 (not_9_out, d_ff_3_q[1]);
  not not_10 (not_10_out, d_ff_3_q[0]);
  and and_26 (and_26_out, xEnd, byP2, not_10_out, not_9_out, d_ff_3_q[2]);
  or or_6 (or_6_out, and_12_out, and_26_out, and_25_out, and_14_out, and_15_out, and_16_out);
  and and_27 (and_27_out, and_2_out, byP1, ~byP2);  // AND_Gate
  and and_28 (and_28_out, ~xEnd, ~xBegin, ~d_ff_3_q[2], d_ff_3_q[1], d_ff_3_q[0]);  // AND_Gate
  and and_29 (and_29_out, and_21_out, score);
  or or_7 (or_7_out, and_21_out, and_5_out, and_6_out, and_22_out, and_30_out, and_32_out);
  and and_30 (and_30_out, or_4_out, and_8_out);
  // AND_Gate and_31 has open pins: in0=d_ff_3_q[2], in1=not_8_out, in2=not_7_out, in3=or_5_out, out=open
  and and_32 (and_32_out, ~d_ff_3_q[2], d_ff_3_q[1], not_7_out, ~byP2, xEnd);  // AND_Gate
  or or_8 (or_8_out, and_27_out, and_18_out, and_1_out, and_3_out, and_4_out, and_20_out, and_28_out, and_5_out, and_29_out);
  Decoder #(.select(3), .enable("false")) decoder_1 (
    .out0(state0), .out1(state1), .out2(state2), .out3(state3), .out4(state4), .out5(state5), .out6(state6),
    .out7(state7), .sel(d_ff_3_q));
  D_Flip_Flop d_ff_1 (.clk(clock_out), .D(or_6_out), .Q(d_ff_3_q[2]));  // open: Qn, preset, en, reset
  D_Flip_Flop d_ff_2 (.clk(clock_out), .D(or_8_out), .Q(d_ff_3_q[1]));  // open: Qn, preset, en, reset
  D_Flip_Flop d_ff_3 (.clk(clock_out), .D(or_7_out), .Q(d_ff_3_q[0]));  // open: Qn, preset, en, reset
  or or_9 (state2_3, state2, state3);
  nor nor_1 (scoreStop, state4, state5);
  or or_10 (or_10_out, state7, state0);
  Multiplexer multiplexer_1 (.in0(1'b1), .in1(Win), .out(multiplexer_1_out), .sel(or_10_out));  // open: en
  Clock clock (.out(clock_out));
  not not_11 (byP1, or_11_out);
  or or_11 (or_11_out, and_33_out[9], and_33_out[8], and_33_out[7], and_33_out[6], and_33_out[5], and_33_out[3], and_33_out[2], and_33_out[1], and_33_out[0], and_33_out[4]);
  assign and_33_out = demultiplexer_1_out1 & players_1_outp2;  // AND_Gate and_33, 10 bits wide
  LED led_1 (.in(or_12_out));
  Counter #(.width(4), .max('hf)) counter_1 (
    .Q(counter_1_q), .clk(state4), .clr(state7));  // open: load, D, count, carry
  or or_12 (or_12_out, comparator_1_eq, state4);
  or or_13 (score, comparator_4_eq, comparator_1_eq);
  Comparator #(.width(4), .mode("unsigned")) comparator_1 (
    .a(4'b1010), .b(counter_1_q), .eq(comparator_1_eq));  // open: gt, lt
  not not_12 (byP2, or_14_out);
  or or_14 (or_14_out, and_34_out[9], and_34_out[8], and_34_out[7], and_34_out[6], and_34_out[5], and_34_out[3], and_34_out[2], and_34_out[1], and_34_out[0], and_34_out[4]);
  assign and_34_out = demultiplexer_1_out18 & or_17_out;  // AND_Gate and_34, 10 bits wide
  and and_35 (and_35_out, multiplexer_1_out, clock_out);
  LED led_2 (.in(or_15_out));
  or or_15 (or_15_out, comparator_4_eq, state5);
  Counter #(.width(4), .max('ha)) counter_2 (
    .Q(counter_2_q), .clk(state5), .clr(state7));  // open: load, D, count, carry
  Clock clock_2 (.out(clock_2_out));
  Comparator #(.width(5), .mode("unsigned")) comparator_2 (
    .a(5'b00001), .b(register_1_q), .eq(xBegin), .lt(comparator_2_lt));  // open: gt
  Comparator #(.width(5), .mode("unsigned")) comparator_3 (
    .a(register_1_q), .b(5'b10010), .eq(xEnd), .lt(loop1));  // open: gt
  Comparator #(.width(4), .mode("unsigned")) comparator_4 (
    .a(4'b1010), .b(counter_2_q), .eq(comparator_4_eq));  // open: gt, lt
  Keyboard keyboard_1 (.re(in_3), .clr(clock_2_out), .data(out_15));  // open: clk, avail
  not not_13 (not_13_out, comparator_2_lt);
  xor xor_1 (xor_1_out, not_13_out, xEnd);
  Counter #(.width(1), .max('h1)) counter_3 (
    .D(xor_1_out), .Q(counter_3_q), .clk(xor_1_out), .clr(state6));  // open: load, count, carry
  and and_36 (and_36_out, ~state4, counter_3_q);  // AND_Gate
  Counter #(.width(5), .max('h13), .ongoal("load")) countBall_X (
    .load(and_36_out), .Q(countBall_X_q), .clk(and_37_out), .clr(state4));  // open: D, count, carry
  and and_37 (and_37_out, and_35_out, ~state4);  // AND_Gate
  // OR_Gate or_16 has open pins: in0=state2_3, in1=state1, out=open
  Players players_1 (.In(out_15), .OutP1(players_1_outp1), .OutP2(players_1_outp2));
  Register #(.width(5), .trigger("high")) register_1 (
    .D(countBall_X_q), .en(and_37_out), .Q(register_1_q), .clk(and_37_out));  // open: clr
  Counter #(.width(4), .max('h9), .ongoal("load")) countBall_Y (
    .D(4'b0001), .Q(countBall_Y_q), .clk(and_35_out));  // open: load, count, carry, clr
  DotMatrix #(.matrixcols(20), .matrixrows(10)) dotmatrix_1 (
    .col0(players_1_outp1), .col1(demultiplexer_1_out1), .col2(demultiplexer_1_out2),
    .col3(demultiplexer_1_out3), .col4(demultiplexer_1_out4), .col5(demultiplexer_1_out5),
    .col6(demultiplexer_1_out6), .col7(demultiplexer_1_out7), .col8(demultiplexer_1_out8),
    .col9(demultiplexer_1_out9), .col10(demultiplexer_1_out10), .col11(demultiplexer_1_out11),
    .col12(demultiplexer_1_out12), .col13(demultiplexer_1_out13), .col14(demultiplexer_1_out14),
    .col15(demultiplexer_1_out15), .col16(demultiplexer_1_out16), .col17(demultiplexer_1_out17),
    .col18(demultiplexer_1_out18), .col19(or_17_out));
  Multiplexer #(.width(4), .enable("false")) multiplexer_2 (.in1(4'b0101), .sel(state0));  // open: in0, out
  Comparator #(.width(10), .mode("unsigned")) comparator_5 (
    .a(10'h1), .b(multiplexer_4_out), .eq(yBegin), .lt(comparator_5_lt));  // open: gt
  not not_14 (not_14_out, comparator_5_lt);
  Comparator #(.width(10), .mode("unsigned")) comparator_6 (
    .a(multiplexer_4_out), .b(10'h200), .eq(yEnd));  // open: gt, lt
  Shifter #(.width(10)) shifter_1 (.in(10'h1), .\dist (countBall_Y_q), .out(shifter_1_out));
  Shifter #(.width(10), .shift("lr")) shifter_2 (.in(10'h200), .\dist (countBall_Y_q), .out(shifter_2_out));
  Button button_1 (.out(reset));
  assign or_17_out = demultiplexer_1_out19 | players_1_outp2;  // OR_Gate or_17, 10 bits wide
  Demultiplexer #(.select(5), .width(10), .enable("false")) demultiplexer_1 (
    .out1(demultiplexer_1_out1), .out2(demultiplexer_1_out2), .out3(demultiplexer_1_out3),
    .out4(demultiplexer_1_out4), .out5(demultiplexer_1_out5), .out6(demultiplexer_1_out6),
    .out7(demultiplexer_1_out7), .out8(demultiplexer_1_out8), .out9(demultiplexer_1_out9),
    .out10(demultiplexer_1_out10), .out11(demultiplexer_1_out11), .out12(demultiplexer_1_out12),
    .out13(demultiplexer_1_out13), .out14(demultiplexer_1_out14), .out15(demultiplexer_1_out15),
    .out16(demultiplexer_1_out16), .out17(demultiplexer_1_out17), .out18(demultiplexer_1_out18),
    .out19(demultiplexer_1_out19), .in(multiplexer_4_out), .sel(register_1_q));  // open: out0, out20, out21, out22, out23, out24, out25, out26, out27, out28, out29, out30, out31
  not not_15 (by, counter_4_q);
  xor xor_2 (xor_2_out, not_14_out, yEnd);
  Counter #(.width(1), .max('h1)) counter_4 (
    .D(xor_2_out), .Q(counter_4_q), .clk(xor_2_out));  // open: load, count, carry, clr
  Multiplexer #(.width(10), .enable("false")) multiplexer_3 (
    .in0(shifter_1_out), .in1(shifter_2_out), .out(multiplexer_3_out), .sel(counter_4_q));
  Register #(.width(10)) ball_Y (.D(multiplexer_3_out), .en(and_35_out), .Q(ball_Y_q), .clk(and_35_out));  // open: clr
  Register #(.width(10)) ball_Y_2 (.D(ball_Y_q), .Q(ball_Y_2_q), .clk(and_35_out));  // open: en, clr
  Multiplexer #(.width(10), .enable("false")) multiplexer_4 (
    .in0(ball_Y_q), .in1(ball_Y_2_q), .out(multiplexer_4_out), .sel(state4));
  Button button_2 (.out(button_2_out));
  Clock clock_3 (.out(clock_3_out));
  Counter #(.width(1), .max('h1)) counter_5 (
    .count(button_2_out), .Q(counter_5_q), .clk(clock_3_out), .clr(counter_5_q));  // open: load, D, carry
  _7_Segment_Display u_7_segment_display_1 (.g(S4), .f(S3), .a(S2), .b(S1), .e(S5), .d(S6), .c(S7));  // open: dp
  SEGMENTOS segmentos_1 (
    ._0(_0), ._1(_1), ._2(_2), ._3(_3), ._4(_4), ._5(_5), ._6(_6), ._7(_7), ._8(_8), ._9(_9),
    .CLOCK(counter_5_q), .out_14(S1), .out_15(S2), .out_16(S3), .out_17(S4), .out_18(S5), .out_19(S6),
    .out_20(S7), .ENABLE(in_13));  // open: reset, out_21

  // Other names for the same wires on the sheet: go = in_1

  // Notes on the sheet:
  //   P2
  //   P1
  //   P0
  //   reset
  //   N2
  //   N1
  //   N0
  //   ball_Y != P1
  //   reset
  //   go
  //   player2_Score
  //   player1_Score
  //   ball_Y != P2
  //   shift_X
  //   clearCountY
  //   clearCountX
  //   random
  //   0000000001
  //   1000000000
  //   shift_up
  //   shift_bottom
  //   ball_Y1
  //   shift_Y
endmodule

module Players (
  input  [6:0] In,
  output [9:0] OutP1,
  output [9:0] OutP2
);

  wire \direção_1_enable , \direção_1_out , \direção_2_enable , \direção_2_out , DownP1, DownP2, UpP1, UpP2;

  Comparator #(.width(7)) comparator_1 (.a(7'b1110111), .b(In), .eq(UpP1));  // open: gt, lt
  Comparator #(.width(7)) comparator_2 (.a(7'b1110011), .b(In), .eq(DownP1));  // open: gt, lt
  Comparator #(.width(7)) comparator_3 (.a(7'b1101111), .b(In), .eq(UpP2));  // open: gt, lt
  Comparator #(.width(7)) comparator_4 (.a(7'b1101100), .b(In), .eq(DownP2));  // open: gt, lt
  \Direção  \direção_1  (.Up_In(UpP1), .Down_In(DownP1), .Out(\direção_1_out ), .Enable(\direção_1_enable ));
  \Direção  \direção_2  (.Up_In(UpP2), .Down_In(DownP2), .Out(\direção_2_out ), .Enable(\direção_2_enable ));
  Movimento movimento_1 (.In(\direção_1_out ), .Enable(\direção_1_enable ), .Out(OutP1));
  Movimento movimento_2 (.In(\direção_2_out ), .Enable(\direção_2_enable ), .Out(OutP2));

  // Notes on the sheet:
  //   W
  //   S
  //   O
  //   L
endmodule

module \Direção  (
  input  Up_In,
  input  Down_In,
  output Out,
  output Enable
);

  wire and_1_out, xor_1_out;

  or or_1 (Enable, Up_In, Down_In);
  xor xor_1 (xor_1_out, Up_In, Down_In);
  and and_1 (and_1_out, Up_In, ~Down_In);  // AND_Gate
  and and_2 (Out, xor_1_out, and_1_out);
endmodule

module Movimento (
  input  In,
  input  Enable,
  output [9:0] Out
);

  wire and_3_out, clock_1_out, comparator_1_lt, comparator_2_lt, d_ff_1_q, not_1_out;
  wire [0:0] and_1_out, and_2_out;
  wire [9:0] multiplexer_1_out, multiplexer_2_out, multiplexer_3_out, shifter_1_out, shifter_2_out;

  Clock clock_1 (.out(clock_1_out));
  not not_1 (not_1_out, In);
  and and_1 (and_1_out[0], In, Enable);
  and and_2 (and_2_out[0], not_1_out, Enable);
  D_Flip_Flop d_ff_1 (.clk(clock_1_out), .D(clock_1_out), .Q(d_ff_1_q));  // open: Qn, preset, en, reset
  Multiplexer #(.width(10), .enable("false")) multiplexer_1 (
    .in0(multiplexer_2_out), .in1(Out), .out(multiplexer_1_out), .sel(and_2_out[0]));
  Multiplexer #(.width(10), .enable("false")) multiplexer_2 (
    .in0(10'hf), .in1(Out), .out(multiplexer_2_out), .sel(d_ff_1_q));
  Shifter #(.width(10), .shift("lr")) shifter_1 (
    .in(multiplexer_1_out), .\dist ({3'b000, and_2_out[0]}), .out(shifter_1_out));
  Multiplexer #(.width(10), .enable("false")) multiplexer_3 (
    .in0(shifter_1_out), .in1(shifter_2_out), .out(multiplexer_3_out), .sel(and_1_out[0]));
  Shifter #(.width(10)) shifter_2 (.in(multiplexer_2_out), .\dist ({3'b000, and_1_out[0]}), .out(shifter_2_out));
  Comparator #(.width(10)) comparator_1 (.a(10'h7), .b(shifter_1_out), .lt(comparator_1_lt));  // open: gt, eq
  Comparator #(.width(10)) comparator_2 (.a(10'h380), .b(shifter_2_out), .lt(comparator_2_lt));  // open: gt, eq
  and and_3 (and_3_out, comparator_1_lt, comparator_2_lt);
  Register #(.width(10)) register_1 (.D(multiplexer_3_out), .en(and_3_out), .Q(Out), .clk(clock_1_out));  // open: clr
endmodule

module SEGMENTOS (
  input  [7:0] _0,
  input  [7:0] _1,
  input  [7:0] _2,
  input  [7:0] _3,
  input  [7:0] _4,
  input  [7:0] _5,
  input  [7:0] _6,
  input  [7:0] _7,
  input  [7:0] _8,
  input  [7:0] _9,
  input  ENABLE,
  input  CLOCK,
  input  reset,
  output out_14,
  output out_15,
  output out_16,
  output out_17,
  output out_18,
  output out_19,
  output out_20,
  output out_21
);

  wire and_1_out, or_1_out;
  wire [3:0] counter_1_q, multiplexer_2_out;

  Counter #(.width(4), .max('hf)) counter_1 (
    .count(CLOCK), .Q(counter_1_q), .clk(CLOCK), .clr(or_1_out));  // open: load, D, carry
  or or_1 (or_1_out, reset, and_1_out);
  Multiplexer #(.select(4), .width(8)) multiplexer_1 (
    .in0(_0), .in1(_1), .in2(_2), .in3(_3), .in4(_4), .in5(_5), .in6(_6), .in7(_7), .in8(_8), .in9(_9),
    .out({out_21, out_20, out_19, out_18, out_17, out_16, out_15, out_14}), .sel(counter_1_q), .en(ENABLE));  // open: in10, in11, in12, in13, in14, in15
  Multiplexer #(.select(4), .width(4)) multiplexer_2 (
    .in10(counter_1_q), .out(multiplexer_2_out), .sel(counter_1_q), .en(ENABLE));  // open: in0, in1, in2, in3, in4, in5, in6, in7, in8, in9, in11, in12, in13, in14, in15
  and and_1 (and_1_out, ~multiplexer_2_out[0], multiplexer_2_out[1], ~multiplexer_2_out[2], multiplexer_2_out[3]);  // AND_Gate
endmodule
